# Fritzing sketch light2-extender-breadboard-wiring-draft (saved by Fritzing 1.0.1rc)
breadboards: 1

parts:
  P4DevKit1 = Olimex ESP32-P4-DevKit Rev D1
  AgonEvenHeader1 = Agon Light 2 even 16-contact header
  AgonOddHeader1 = Agon Light 2 odd 16-contact header
  AgonOddPinLabelBank1 = Agon Light 2 odd pin-label bank  # not connected
  AgonEvenPinLabelBank1 = Agon Light 2 even pin-label bank  # not connected
  R1 = Resistor [tolerance=±5% power=0.25 resistance=220 package=THT]
  R2 = Resistor [tolerance=±5% power=0.25 resistance=220 package=THT]
  R3 = Resistor [tolerance=±5% power=0.25 resistance=220 package=THT]
  R4 = Resistor [tolerance=±5% power=0.25 resistance=220 package=THT]
  R5 = Resistor [tolerance=±5% power=0.25 resistance=220 package=THT]
  R6 = Resistor [tolerance=±5% power=0.25 resistance=220 package=THT]
  R7 = Resistor [tolerance=±5% power=0.25 resistance=220 package=THT]
  R8 = Resistor [tolerance=±5% power=0.25 resistance=10000 package=THT]
  R9 = Resistor [tolerance=±5% power=0.25 resistance=220 package=THT]
  R10 = Resistor [tolerance=±5% power=0.25 resistance=10000 package=THT]
  C1 = Ceramic Capacitor [capacitance=100nF voltage=35V package="100 mil [THT, multilayer]"]
  R11 = Resistor [tolerance=±5% power=0.25 resistance=220 package=THT]
  R12 = Resistor [tolerance=±5% power=0.25 resistance=10000 package=THT]
  R14 = Resistor [tolerance=±5% power=0.25 resistance=10000 package=THT]
  R15 = Resistor [tolerance=±5% power=0.25 resistance=10000 package=THT]
  R13 = Resistor [tolerance=±5% power=0.25 resistance=10000 package=THT]

nets:
  N1: P4DevKit1.EXT1_pin_10_—_GPIO9, R1.Pin_0
  N2: P4DevKit1.EXT1_pin_11_—_GPIO10, R2.Pin_0
  N3: P4DevKit1.EXT1_pin_12_—_GPIO11, R3.Pin_0
  N4: P4DevKit1.EXT1_pin_13_—_GPIO12, R9.Pin_1
  N5: P4DevKit1.EXT1_pin_14_—_GPIO13, AgonEvenHeader1.Agon_pin_16_—_PD7, R15.Pin_1
  N6: P4DevKit1.EXT1_pin_15_—_GPIO14, AgonEvenHeader1.Agon_pin_14_—_PD5_/_CTS1, R13.Pin_1
  N7: P4DevKit1.EXT1_pin_16_—_GPIO15, R10.Pin_0
  N8: P4DevKit1.EXT2_pin_8_—_GPIO33, R4.Pin_1
  N9: P4DevKit1.EXT2_pin_9_—_GPIO32, R5.Pin_1
  N10: P4DevKit1.EXT2_pin_10_—_GPIO23, R6.Pin_1
  N11: P4DevKit1.EXT2_pin_11_—_GPIO22, R11.Pin_0
  N12: P4DevKit1.EXT2_pin_12_—_GPIO21, R8.Pin_0
  N13: P4DevKit1.EXT2_pin_13_—_GPIO20, AgonOddHeader1.Agon_pin_13_—_PD4_/_RTS1, R14.Pin_0
  N14: AgonEvenHeader1.Agon_pin_18_—_PC1, R7.Pin_0
  N15: AgonEvenHeader1.Agon_pin_20_—_PC3, R3.Pin_1
  N16: AgonEvenHeader1.Agon_pin_22_—_PC5, R2.Pin_1
  N17: AgonEvenHeader1.Agon_pin_24_—_PC7, R1.Pin_1
  N18: AgonOddHeader1.Agon_pin_19_—_PC2_/_TXD1, R6.Pin_0
  N19: AgonOddHeader1.Agon_pin_21_—_PC4, R5.Pin_0
  N20: AgonOddHeader1.Agon_pin_23_—_PC6, R4.Pin_0
  N21: C1.0, C1.1, R13.Pin_0
  N22: R12.Pin_0, R14.Pin_1, R15.Pin_0

custom parts:
  Olimex ESP32-P4-DevKit Rev D1: Diagrammatic Rev D1 breadboard representation generated from official Olimex EXT1/EXT2 geometry for SETUP-006.3; the rendered body is deliberately cropped to expose adjacent breadboard sockets.
  Agon Light 2 even 16-contact header: Label-free Agon Light 2 even 16-contact harness bank. Physical pins 33 and 34 are intentionally excluded; their separate wiring is not drawn. Labels are separate movable diagram objects.
  Agon Light 2 odd 16-contact header: Label-free Agon Light 2 odd 16-contact harness bank. Physical pins 33 and 34 are intentionally excluded; their separate wiring is not drawn. Labels are separate movable diagram objects.
  Agon Light 2 odd pin-label bank: One independently movable, color-coded odd bank containing exactly 16 represented Agon Light 2 pin labels on 0.1-inch row pitch; contains no Extender-specific functional mappings.
  Agon Light 2 even pin-label bank: One independently movable, color-coded even bank containing exactly 16 represented Agon Light 2 pin labels on 0.1-inch row pitch; contains no Extender-specific functional mappings.
