# Fritzing sketch light2-extender-breadboard-wiring-draft_v2 (saved by Fritzing 1.0.1rc)
breadboards: 1

parts:
  P4DevKit1 = Olimex ESP32-P4-DevKit Rev D1
  AgonEvenHeader1 = Agon Light 2 even 16-contact header
  AgonOddHeader1 = Agon Light 2 odd 16-contact header
  AgonOddPinLabelBank1 = Agon Light 2 odd pin-label bank  # not connected
  AgonEvenPinLabelBank1 = Agon Light 2 even pin-label bank  # not connected
  R1 = Resistor [tolerance=±5% power=0.25 resistance=220 package=THT]
  R2 = Resistor [tolerance=±5% power=0.25 resistance=220 package=THT]
  R3 = Resistor [tolerance=±5% power=0.25 resistance=220 package=THT]
  R4 = Resistor [tolerance=±5% power=0.25 resistance=220 package=THT]
  R5 = Resistor [tolerance=±5% power=0.25 resistance=220 package=THT]
  R6 = Resistor [tolerance=±5% power=0.25 resistance=220 package=THT]
  R7 = Resistor [tolerance=±5% power=0.25 resistance=220 package=THT]
  R8 = Resistor [tolerance=±5% power=0.25 resistance=10000 package=THT]
  R9 = Resistor [tolerance=±5% power=0.25 resistance=220 package=THT]
  R10 = Resistor [tolerance=±5% power=0.25 resistance=10000 package=THT]
  C1 = Ceramic Capacitor [capacitance=100nF voltage=35V package="100 mil [THT, multilayer]"]
  R11 = Resistor [tolerance=±5% power=0.25 resistance=220 package=THT]
  R12 = Resistor [tolerance=±5% power=0.25 resistance=10000 package=THT]
  R14 = Resistor [tolerance=±5% power=0.25 resistance=10000 package=THT]
  R15 = Resistor [tolerance=±5% power=0.25 resistance=10000 package=THT]
  R13 = Resistor [tolerance=±5% power=0.25 resistance=10000 package=THT]
  U1 = SN74HC125N quad tri-state buffer [part_number=SN74HC125N package="DIP-14 (diagrammatic breadboard view)"]
  AgonPin34ThreeV3_1 = Agon pin 34 +3.3 V
  AgonPin33Ground1 = Agon pin 33 GND

nets:
  N1: P4DevKit1.EXT1_pin_2_—_GND, C1.0, R13.Pin_0, U1.pin_7_GND, U1.pin_9_3A, AgonPin33Ground1.Agon_pin_33_GND
  N2: P4DevKit1.EXT1_pin_10_—_GPIO9, R1.Pin_0
  N3: P4DevKit1.EXT1_pin_11_—_GPIO10, R2.Pin_0
  N4: P4DevKit1.EXT1_pin_12_—_GPIO11, R3.Pin_0
  N5: P4DevKit1.EXT1_pin_13_—_GPIO12, R9.Pin_1, U1.pin_5_2A
  N6: P4DevKit1.EXT1_pin_14_—_GPIO13, AgonEvenHeader1.Agon_pin_16_—_PD7, R15.Pin_1
  N7: P4DevKit1.EXT1_pin_15_—_GPIO14, AgonEvenHeader1.Agon_pin_14_—_PD5, R13.Pin_1
  N8: P4DevKit1.EXT1_pin_16_—_GPIO15, R10.Pin_0, U1.pin_1_1OE_N, U1.pin_13_4OE_N
  N9: P4DevKit1.EXT2_pin_8_—_GPIO33, R4.Pin_1
  N10: P4DevKit1.EXT2_pin_9_—_GPIO32, R5.Pin_1
  N11: P4DevKit1.EXT2_pin_10_—_GPIO23, R6.Pin_1
  N12: P4DevKit1.EXT2_pin_11_—_GPIO22, R11.Pin_0
  N13: P4DevKit1.EXT2_pin_12_—_GPIO21, R8.Pin_0, U1.pin_4_2OE_N
  N14: P4DevKit1.EXT2_pin_13_—_GPIO20, AgonOddHeader1.Agon_pin_13_—_PD4, R14.Pin_0
  N15: AgonEvenHeader1.Agon_pin_18_—_PC1_/_RXD1, R7.Pin_0, U1.pin_2_1A
  N16: AgonEvenHeader1.Agon_pin_20_—_PC3_/_CTS1, R3.Pin_1
  N17: AgonEvenHeader1.Agon_pin_22_—_PC5, R2.Pin_1
  N18: AgonEvenHeader1.Agon_pin_24_—_PC7, R1.Pin_1
  N19: AgonOddHeader1.Agon_pin_17_—_PC0_/_TXD1, U1.pin_12_4A
  N20: AgonOddHeader1.Agon_pin_19_—_PC2_/_RTS1, R6.Pin_0
  N21: AgonOddHeader1.Agon_pin_21_—_PC4, R5.Pin_0
  N22: AgonOddHeader1.Agon_pin_23_—_PC6, R4.Pin_0
  N23: R7.Pin_1, U1.pin_6_2Y
  N24: R8.Pin_1, R10.Pin_1, C1.1, R12.Pin_0, R14.Pin_1, R15.Pin_0, U1.pin_14_VCC, AgonPin34ThreeV3_1.Agon_pin_34_+3.3_V
  N25: R9.Pin_0, U1.pin_3_1Y
  N26: R11.Pin_1, U1.pin_11_4Y
  N27: R12.Pin_1, U1.pin_10_3OE_N

custom parts:
  Olimex ESP32-P4-DevKit Rev D1: Diagrammatic Rev D1 breadboard representation generated from official Olimex EXT1/EXT2 geometry for SETUP-006.3; the rendered body is deliberately cropped to expose adjacent breadboard sockets.
  Agon Light 2 even 16-contact header: Label-free Agon Light 2 even 16-contact harness bank. Physical pins 33 and 34 are intentionally excluded; their separate wiring is not drawn. Labels are separate movable diagram objects.
  Agon Light 2 odd 16-contact header: Label-free Agon Light 2 odd 16-contact harness bank. Physical pins 33 and 34 are intentionally excluded; their separate wiring is not drawn. Labels are separate movable diagram objects.
  Agon Light 2 odd pin-label bank: One independently movable, color-coded odd bank containing exactly 16 represented Agon Light 2 pin labels on 0.1-inch row pitch; contains no Extender-specific functional mappings.
  Agon Light 2 even pin-label bank: One independently movable, color-coded even bank containing exactly 16 represented Agon Light 2 pin labels on 0.1-inch row pitch; contains no Extender-specific functional mappings.
  SN74HC125N quad tri-state buffer: Task-local wiring-diagram representation of the documented on-hand SN74HC125N U1. Transverse artwork is compressed to the accepted breadboard scaffold and is not package or PCB geometry.
  Agon pin 34 +3.3 V: Separate red 3.3 V logic-reference lead from Agon Light 2 physical pin 34.
  Agon pin 33 GND: Separate black ground lead from Agon Light 2 physical pin 33.
